# Fritzing sketch ARDUINO (saved by Fritzing 0.9.3b)
breadboards: 1

parts:
  Componente1 = Arduino Uno (Rev3)
  LCD1 = LCD screen
  R1 = Rotary Potentiometer (Small) [maximum_resistance=100kΩ package=THT]
  R3 = Temperature Sensor (Thermistor) [thermistor_type=NTC package=THT]
  R4 = Resistor [tolerance=±5% resistance=220 package=THT]

nets:
  N1: Componente1.A0, R3.pin_1, R4.Pin_0
  N2: Componente1.D8, LCD1.E
  N3: Componente1.D9_PWM, LCD1.DB4
  N4: Componente1.D10_PWM/SS, LCD1.DB5
  N5: Componente1.D11_PWM/MOSI, LCD1.DB6
  N6: Componente1.D12/MISO, LCD1.DB7
  N7: Componente1.D7, LCD1.RS
  5V: Componente1.5V, LCD1.VDD, LCD1.LED+, R1.leg1, R3.pin_0
  GND: Componente1.GND, LCD1.VSS, LCD1.R/W, LCD1.LED-, R1.leg2, R4.Pin_1
  N8: LCD1.V0, R1.wiper

// code stored in the sketch: ArduinoDisplay.ino
//import libraries
#include <LiquidCrystal.h>


//define object and pin utilized
LiquidCrystal lcd(7, 8, 9, 10, 11, 12);



void setup()
{
  // set up the LCD's number of columns and rows:
  lcd.begin(16, 2);
  Serial.begin(9600);
}



void loop()
{
  while(Serial.available()>0){
    //receive from node-RED a string containing the alarmCode and the temperature
    String reading=Serial.readString();
    //generate two different substring for the two values
    int firstIndex = reading.indexOf("-");
    String firstSubstring = reading.substring(0, firstIndex);
    int alarmCode=firstSubstring.toInt();
    int secondIndex = reading.indexOf("-", firstIndex + 1);
    String temperature = reading.substring(firstIndex + 1, secondIndex);


    Serial.println(alarmCode);
    Serial.println(temperature);
    long starttime = millis(); //timer to utilize in the display
    long endtime = starttime;
    switch(alarmCode){ //based on the alarm code, different messages are displayed
      case 1:   //Abnormal Temperature      
        while ((endtime - starttime) <=5000){// do this loop for up to 5000mS
          lcd.print("    " + temperature + " " +  ((char)223) + "C" );          
          lcd.setCursor(0, 1);
          lcd.print("     ALARM!     ");     
          delay(500);     
          lcd.clear();
          delay(500);
          lcd.print("ABNORMAL");
          lcd.setCursor(0, 1);
          lcd.print("TEMPERATURE");
          delay(500);
          lcd.clear();
          delay(500);
          endtime = millis();
        }
        break;
      case 2:   //Increasing Temperature 
        while ((endtime - starttime) <=5000){// do this loop for up to 5000mS
          lcd.print("    " + temperature + " " +  ((char)223) + "C" );          
          lcd.setCursor(0, 1);
          lcd.print("     ALARM!     ");     
          delay(500);     
          lcd.clear();
          delay(500);
          lcd.print("INCREASING");
          lcd.setCursor(0, 1);
          lcd.print("TEMPERATURE");
          delay(500);
          lcd.clear();
          delay(500);
          endtime = millis();        
        }
        break;
      case 3:   //Spike of Temperature
        while ((endtime - starttime) <=5000){// do this loop for up to 5000mS
          lcd.print("    " + temperature + " " +  ((char)223) + "C" );          
          lcd.setCursor(0, 1);
          lcd.print("     ALARM!     ");     
          delay(500);     
          lcd.clear();
          delay(500);
          lcd.print("SPIKE OF");
          lcd.setCursor(0, 1);
          lcd.print("TEMPERATURE");
          delay(500);
          lcd.clear();
          delay(500);
          endtime = millis();
        }
        break;
      case 0:   //Normal reading with no alarm
        while ((endtime - starttime) <=2000){// do this loop for up to 2000mS
          lcd.print("    " + temperature + " " +  ((char)223) + "C" );          
          lcd.setCursor(0, 1);
          lcd.print("      !OK!    ");
          endtime = millis();
        }
        break;
    }
  }
  lcd.clear();  
}
